# Fritzing sketch FPHO3B5IYOQ48DA (saved by Fritzing 0.9.2b)
breadboards: 1

parts:
  Part2 = Photon
  U1 = LIPO-1000mAh [package=lipo-1000]
  part = electronicsguy 0.96" 128x64 SPI I2C OLED

nets:
  GND: Part2.A0, Part2.A1, Part2.A3, Part2.A4, Part2.A5, Part2.DAC, Part2.WKP, Part2.TX, Part2.GND, Part2.VIN, U1.+, U1.-, part.GND, part.D1, part.D0
  N1: Part2.D3, part.DC
  N2: Part2.D4, part.CS
  N3: Part2.D5, part.RST
  3V3: Part2.3V3, part.VCC

custom parts:
  electronicsguy 0.96" 128x64 SPI I2C OLED: Generic 0.96" 128x64 SPI I2C OLED Default is SPI mode Can be re-configured for I2C (needs soldering work) Comes in various colors like blue, white, yellow-blue
